# Fritzing sketch project_circuit (saved by Fritzing 0.9.3b)
breadboards: 2

parts:
  Mod1 = Raspberry Pi Pico W
  U1 = Voltage Regulator - Variable [package="TO220 [THT]"]
  V1 = DC Power [voltage=12V]
  C1 = Capacitor [package=cap-pth-small]
  R1 = Resistor [tolerance=±5% resistance=220 package="0402 [SMD]"]
  R3 = Rotary Potentiometer (Large) [maximum_resistance=100kΩ package=THT]
  C2 = Capacitor Polarized [package=panasonic_c]
  M1 = DC Motor
  OMRON1 = OMRON PCB Power Relay – G5LE [part_number="G5LE-1\n" package=THT]
  Power_plug1 = Power plug

nets:
  N1: Mod1.pin_1, OMRON1.C
  N2: Mod1.pin_3, Mod1.pin_8, Mod1.pin_13, Mod1.pin_18, Mod1.pin_23, Mod1.pin_28, Mod1.pin_33, Mod1.pin_38
  N3: Mod1.pin_39, U1.OUT, R1.Pin_1, C2.+
  N4: U1.ADJ, R3.leg1
  N5: U1.IN, V1.V+, C1.1, OMRON1.COIL2, Power_plug1.VCC
  GND: V1.V-, C1.2, R3.leg2, C2.-, M1.pin_2, OMRON1.COIL1, Power_plug1.GND
  N6: R1.Pin_0, R3.wiper
  N7: M1.pin_1, OMRON1.B

custom parts:
  Raspberry Pi Pico W: Raspberry Pi Pico W. Based around the RP2040 microcontroller the Pico W is a low cost microcontroller device bringing Raspberry Pi quality, cost, and easy of use to the microcontroller space. The areas marked KEEPOUT in pcb silkscreen should not have traces running through them to avoid shorts on a soldered in module!
